// Logisim project logisim.circ as structural Verilog: 1 circuit, main circuit main
module main (
);

  wire decoder_1_out0, decoder_1_out1, decoder_1_out2, decoder_1_out3, multiplexer_1_out, not_1_out,
       not_2_out, not_3_out, or_1_out, or_2_out, undriven, undriven_4;
  wire [1:0] undriven_2;
  wire [2:0] undriven_3;

  Decoder #(.select(2)) decoder_1 (
    .out0(decoder_1_out0), .out1(decoder_1_out1), .out2(decoder_1_out2), .out3(decoder_1_out3),
    .sel(undriven_2), .en(undriven));
  or or_1 (or_1_out, decoder_1_out2, decoder_1_out3);
  not not_1 (not_1_out, decoder_1_out0);
  not not_2 (not_2_out, decoder_1_out2);
  or or_2 (or_2_out, decoder_1_out0, decoder_1_out1);
  not not_3 (not_3_out, or_1_out);
  Multiplexer #(.select(3)) multiplexer_1 (
    .in0(or_1_out), .in1(not_1_out), .in2(or_2_out), .in3(not_2_out), .in4(decoder_1_out2), .in5(not_2_out),
    .in6(1'b0), .in7(not_3_out), .out(multiplexer_1_out), .sel(undriven_3), .en(undriven_4));

  // Notes on the sheet:
  //   y1, y0
  //   x2, x1, x0
  //   z
endmodule
